// Logisim project 32x32-bit-register-file.circ as structural Verilog: 1 circuit, main circuit main
module main (
  input  in_1,
  input  in_2,
  input  in_3,
  input  in_4,
  input  RW,
  input  RegWrite
);

  wire _1_out, _2_out, _3_out, _4_out, _5_out, _6_out, _7_out, _8_out, _9_out, _10_out, _11_out, _12_out,
       _13_out, _14_out, _15_out, _16_out, _17_out, _18_out, _19_out, _20_out, _21_out, _22_out, _23_out,
       _24_out, _25_out, _26_out, _27_out, _28_out, _29_out, _30_out, _31_out, clock_1_out, decoder_1_out1,
       decoder_1_out2, decoder_1_out3, decoder_1_out4, decoder_1_out5, decoder_1_out6, decoder_1_out7,
       decoder_1_out8, decoder_1_out9, decoder_1_out10, decoder_1_out11, decoder_1_out12, decoder_1_out13,
       decoder_1_out14, decoder_1_out15, decoder_1_out16, decoder_1_out17, decoder_1_out18, decoder_1_out19,
       decoder_1_out20, decoder_1_out21, decoder_1_out22, decoder_1_out23, decoder_1_out24, decoder_1_out25,
       decoder_1_out26, decoder_1_out27, decoder_1_out28, decoder_1_out29, decoder_1_out30, decoder_1_out31,
       undriven_2;
  wire [31:0] undriven;

  Clock clock_1 (.out(clock_1_out));
  Decoder #(.select(5)) decoder_1 (
    .out1(decoder_1_out1), .out2(decoder_1_out2), .out3(decoder_1_out3), .out4(decoder_1_out4),
    .out5(decoder_1_out5), .out6(decoder_1_out6), .out7(decoder_1_out7), .out8(decoder_1_out8),
    .out9(decoder_1_out9), .out10(decoder_1_out10), .out11(decoder_1_out11), .out12(decoder_1_out12),
    .out13(decoder_1_out13), .out14(decoder_1_out14), .out15(decoder_1_out15), .out16(decoder_1_out16),
    .out17(decoder_1_out17), .out18(decoder_1_out18), .out19(decoder_1_out19), .out20(decoder_1_out20),
    .out21(decoder_1_out21), .out22(decoder_1_out22), .out23(decoder_1_out23), .out24(decoder_1_out24),
    .out25(decoder_1_out25), .out26(decoder_1_out26), .out27(decoder_1_out27), .out28(decoder_1_out28),
    .out29(decoder_1_out29), .out30(decoder_1_out30), .out31(decoder_1_out31),
    .sel({in_1, in_2, in_3, in_4, RW}), .en(1'b1));  // open: out0
  and _25 (_25_out, decoder_1_out25, RegWrite);
  and _26 (_26_out, decoder_1_out26, RegWrite);
  and _27 (_27_out, decoder_1_out27, RegWrite);
  and _28 (_28_out, decoder_1_out28, RegWrite);
  and _29 (_29_out, decoder_1_out29, RegWrite);
  and _30 (_30_out, decoder_1_out30, RegWrite);
  and _31 (_31_out, decoder_1_out31, RegWrite);
  and _17 (_17_out, decoder_1_out17, RegWrite);
  and _18 (_18_out, decoder_1_out18, RegWrite);
  and _19 (_19_out, decoder_1_out19, RegWrite);
  and _20 (_20_out, decoder_1_out20, RegWrite);
  and _21 (_21_out, decoder_1_out21, RegWrite);
  and _22 (_22_out, decoder_1_out22, RegWrite);
  and _23 (_23_out, decoder_1_out23, RegWrite);
  and _24 (_24_out, decoder_1_out24, RegWrite);
  Register #(.width(32)) R25 (.D(undriven), .en(_25_out), .clk(clock_1_out));  // open: Q, clr
  Register #(.width(32)) R26 (.D(undriven), .en(_26_out), .clk(clock_1_out));  // open: Q, clr
  Register #(.width(32)) R27 (.D(undriven), .en(_27_out), .clk(clock_1_out));  // open: Q, clr
  Register #(.width(32)) R28 (.D(undriven), .en(_28_out), .clk(clock_1_out));  // open: Q, clr
  Register #(.width(32)) R29 (.D(undriven), .en(_29_out), .clk(clock_1_out));  // open: Q, clr
  Register #(.width(32)) R30 (.D(undriven), .en(_30_out), .clk(clock_1_out));  // open: Q, clr
  Register #(.width(32)) R31 (.D(undriven), .en(_31_out), .clk(clock_1_out));  // open: Q, clr
  Register #(.width(32)) R17 (.D(undriven), .en(_17_out), .clk(clock_1_out));  // open: Q, clr
  Register #(.width(32)) R18 (.D(undriven), .en(_18_out), .clk(clock_1_out));  // open: Q, clr
  Register #(.width(32)) R19 (.D(undriven), .en(_19_out), .clk(undriven_2));  // open: Q, clr
  Register #(.width(32)) R20 (.D(undriven), .en(_20_out), .clk(clock_1_out));  // open: Q, clr
  Register #(.width(32)) R21 (.D(undriven), .en(_21_out), .clk(clock_1_out));  // open: Q, clr
  Register #(.width(32)) R22 (.D(undriven), .en(_22_out), .clk(clock_1_out));  // open: Q, clr
  Register #(.width(32)) R23 (.D(undriven), .en(_23_out), .clk(clock_1_out));  // open: Q, clr
  Register #(.width(32)) R24 (.D(undriven), .en(_24_out), .clk(clock_1_out));  // open: Q, clr
  and _9 (_9_out, decoder_1_out9, RegWrite);
  and _10 (_10_out, decoder_1_out10, RegWrite);
  and _11 (_11_out, decoder_1_out11, RegWrite);
  and _12 (_12_out, decoder_1_out12, RegWrite);
  and _13 (_13_out, decoder_1_out13, RegWrite);
  and _14 (_14_out, decoder_1_out14, RegWrite);
  and _15 (_15_out, decoder_1_out15, RegWrite);
  and _16 (_16_out, decoder_1_out16, RegWrite);
  and _1 (_1_out, decoder_1_out1, RegWrite);
  and _2 (_2_out, decoder_1_out2, RegWrite);
  and _3 (_3_out, decoder_1_out3, RegWrite);
  and _4 (_4_out, decoder_1_out4, RegWrite);
  and _5 (_5_out, decoder_1_out5, RegWrite);
  and _6 (_6_out, decoder_1_out6, RegWrite);
  and _7 (_7_out, decoder_1_out7, RegWrite);
  and _8 (_8_out, decoder_1_out8, RegWrite);
  Register #(.width(32)) R9 (.D(undriven), .en(_9_out), .clk(clock_1_out));  // open: Q, clr
  Register #(.width(32)) R10 (.D(undriven), .en(_10_out), .clk(clock_1_out));  // open: Q, clr
  Register #(.width(32)) R11 (.D(undriven), .en(_11_out), .clk(clock_1_out));  // open: Q, clr
  Register #(.width(32)) R12 (.D(undriven), .en(_12_out), .clk(clock_1_out));  // open: Q, clr
  Register #(.width(32)) R13 (.D(undriven), .en(_13_out), .clk(clock_1_out));  // open: Q, clr
  Register #(.width(32)) R14 (.D(undriven), .en(_14_out), .clk(clock_1_out));  // open: Q, clr
  Register #(.width(32)) R15 (.D(undriven), .en(_15_out), .clk(clock_1_out));  // open: Q, clr
  Register #(.width(32)) R16 (.D(undriven), .en(_16_out), .clk(clock_1_out));  // open: Q, clr
  Register #(.width(32)) R1 (.D(undriven), .en(_1_out), .clk(clock_1_out));  // open: Q, clr
  Register #(.width(32)) R2 (.D(undriven), .en(_2_out), .clk(clock_1_out));  // open: Q, clr
  Register #(.width(32)) R3 (.D(undriven), .en(_3_out), .clk(clock_1_out));  // open: Q, clr
  Register #(.width(32)) R4 (.D(undriven), .en(_4_out), .clk(clock_1_out));  // open: Q, clr
  Register #(.width(32)) R5 (.D(undriven), .en(_5_out), .clk(clock_1_out));  // open: Q, clr
  Register #(.width(32)) R6 (.D(undriven), .en(_6_out), .clk(clock_1_out));  // open: Q, clr
  Register #(.width(32)) R7 (.D(undriven), .en(_7_out), .clk(clock_1_out));  // open: Q, clr
  Register #(.width(32)) R8 (.D(undriven), .en(_8_out), .clk(clock_1_out));  // open: Q, clr
endmodule
