// Logisim project Pipelined Processor Design.circ as structural Verilog: 3 circuits, main circuit main
module main (
  output [15:0] out_1
);

  wire addi, and_2_out, and_4_out, and_5_out, and_6_out, and_7_out, and_8_out, and_9_out, and_10_out, andi,
       Branch, Clk, comparator_1_gt, decoder_1_out1, j, jal, JALR, JR, lui, lw, not_1_out, not_2_out,
       or_3_out, or_4_out, or_6_out, or_7_out, or_10_out, or_11_out, ori, RegWrite, sw;
  wire [1:0] or_2_out, or_8_out;
  wire [2:0] Func, multiplexer_2_out, multiplexer_3_out, multiplexer_4_out;
  wire [3:0] OpCode;
  wire [5:0] Branch_Instructions;
  wire [11:0] Branch_PC, multiplexer_1_out, PC, PC_1, Sign_Extended12;
  wire [11:3] J_12Im;
  wire [15:0] bit_extender_4_out, DataMemory_Out, multiplexer_5_out, multiplexer_6_out, multiplexer_7_out,
       Rs_Out, Rt_Out, Sign_Extended, Zero_Extended;

  Clock clock_1 (.out(Clk));
  and and_1 (JR, and_2_out, decoder_1_out1);
  and and_2 (and_2_out, Func[2], Func[1], not_1_out);
  not not_1 (not_1_out, Func[0]);
  Adder #(.width(12)) adder_1 (.a(PC), .b(12'h1), .out(PC_1));  // open: cin, cout
  Multiplexer #(.select(2), .width(12), .enable("false")) multiplexer_1 (
    .in0(PC_1), .in1(Rs_Out[11:0]), .in2(Branch_PC), .in3({J_12Im, Func}), .out(multiplexer_1_out),
    .sel(or_2_out));
  or or_1 (or_2_out[1], or_3_out, Branch);
  or or_2 (or_2_out[0], or_4_out, or_3_out);
  or or_3 (or_3_out, j, jal);
  or or_4 (or_4_out, JR, JALR);
  and and_3 (JALR, and_4_out, decoder_1_out1);
  and and_4 (and_4_out, Func[2], Func[1], Func[0]);
  Register #(.width(12)) u_PC (.D(multiplexer_1_out), .en(1'b1), .Q(PC), .clk(Clk));  // open: clr
  Decoder #(.select(4), .enable("false")) decoder_1 (
    .out1(decoder_1_out1), .out2(andi), .out3(ori), .out4(addi), .out5(sw), .out6(lw),
    .out7(Branch_Instructions[0]), .out8(Branch_Instructions[1]), .out9(Branch_Instructions[2]),
    .out10(Branch_Instructions[3]), .out11(Branch_Instructions[4]), .out12(Branch_Instructions[5]),
    .out13(lui), .out14(j), .out15(jal), .sel(OpCode));  // open: out0
  RAM #(.addrWidth(12), .dataWidth(16)) ram_1 (.addr(PC), .data({OpCode, J_12Im, Func}));  // open: sel, clk, ld, clr
  assign Sign_Extended = {{10{J_12Im[5]}}, {J_12Im[5:3], Func}};  // Bit_Extender bit_extender_1
  assign Zero_Extended = {{10{1'b0}}, {J_12Im[5:3], Func}};  // Bit_Extender bit_extender_2
  assign Sign_Extended12 = {{6{J_12Im[5]}}, {J_12Im[5:3], Func}};  // Bit_Extender bit_extender_3
  or or_5 (RegWrite, JR, not_2_out);
  not not_2 (not_2_out, comparator_1_gt);
  Comparator #(.width(11), .mode("unsigned")) comparator_1 (
    .a({1'b0, j, 1'b0, Branch_Instructions, 1'b0, sw}), .b({11{1'b0}}), .gt(comparator_1_gt));  // open: eq, lt
  or or_6 (or_6_out, Branch_Instructions[0], Branch_Instructions[1], Branch_Instructions[2], Branch_Instructions[3], Branch_Instructions[4], Branch_Instructions[5], sw);
  Multiplexer #(.width(3), .enable("false")) multiplexer_2 (
    .in0(3'b111), .in1(3'b001), .out(multiplexer_2_out), .sel(lui));
  or or_7 (or_7_out, jal, lui);
  Multiplexer #(.width(3), .enable("false")) multiplexer_3 (
    .in0(J_12Im[11:9]), .in1(multiplexer_2_out), .out(multiplexer_3_out), .sel(or_7_out));
  Multiplexer #(.width(3), .enable("false")) multiplexer_4 (
    .in0(J_12Im[5:3]), .in1(multiplexer_3_out), .out(multiplexer_4_out), .sel(or_6_out));
  RegisterFile registerfile_1 (
    .BusW(multiplexer_5_out), .Clock(Clk), .RegWrite(RegWrite), .RA(J_12Im[8:6]), .RB(multiplexer_4_out),
    .RW(multiplexer_3_out), .BusA(Rs_Out), .BusB(Rt_Out));
  Multiplexer #(.select(2), .width(16), .enable("false")) multiplexer_5 (
    .in0(out_1), .in1(bit_extender_4_out), .in2(DataMemory_Out), .in3({J_12Im, Func, 4'b0000}),
    .out(multiplexer_5_out), .sel(or_8_out));
  or or_8 (or_8_out[0], JALR, jal, lui);
  or or_9 (or_8_out[1], lw, lui);
  Hex_Digit_Display hex_digit_display_1 (.value(Rs_Out[15:12]));  // open: dp
  Hex_Digit_Display hex_digit_display_2 (.value(Rs_Out[11:8]));  // open: dp
  Hex_Digit_Display hex_digit_display_3 (.value(Rt_Out[15:12]));  // open: dp
  Hex_Digit_Display hex_digit_display_4 (.value(Rt_Out[11:8]));  // open: dp
  assign bit_extender_4_out = {{4{1'b0}}, PC_1};  // Bit_Extender bit_extender_4
  Hex_Digit_Display hex_digit_display_5 (.value(Rs_Out[7:4]));  // open: dp
  Hex_Digit_Display hex_digit_display_6 (.value(Rt_Out[7:4]));  // open: dp
  Hex_Digit_Display hex_digit_display_7 (.value(Rs_Out[3:0]));  // open: dp
  Hex_Digit_Display hex_digit_display_8 (.value(Rt_Out[3:0]));  // open: dp
  or or_10 (or_10_out, addi, sw, lw);
  and and_5 (and_5_out, Branch_Instructions[4], out_1[0]);
  and and_6 (and_6_out, Branch_Instructions[5], out_1[0]);
  Multiplexer #(.width(16), .enable("false")) multiplexer_6 (
    .in0(Rt_Out), .in1(multiplexer_7_out), .out(multiplexer_6_out), .sel(or_11_out));
  Multiplexer #(.width(16), .enable("false")) multiplexer_7 (
    .in0(Zero_Extended), .in1(Sign_Extended), .out(multiplexer_7_out), .sel(or_10_out));
  or or_11 (or_11_out, andi, ori, addi, sw, lw);
  or or_12 (Branch, and_6_out, and_5_out, and_8_out, and_7_out, and_10_out, and_9_out);
  and and_7 (and_7_out, Branch_Instructions[2], out_1[0]);
  and and_8 (and_8_out, Branch_Instructions[3], out_1[0]);
  Adder #(.width(12)) adder_2 (.a(Sign_Extended12), .b(PC), .out(Branch_PC));  // open: cin, cout
  ALU alu_1 (.Op(OpCode), .func(Func), .Rt(multiplexer_6_out), .Rs(Rs_Out), .Rd(out_1));
  and and_9 (and_9_out, Branch_Instructions[0], out_1[0]);
  and and_10 (and_10_out, Branch_Instructions[1], out_1[0]);
  Hex_Digit_Display hex_digit_display_9 (.value(out_1[15:12]));  // open: dp
  Hex_Digit_Display hex_digit_display_10 (.value(out_1[11:8]));  // open: dp
  Hex_Digit_Display hex_digit_display_11 (.value(out_1[7:4]));  // open: dp
  Hex_Digit_Display hex_digit_display_12 (.value(out_1[3:0]));  // open: dp
  RAM #(.addrWidth(16), .dataWidth(16), .bus("separate")) ram_2 (
    .addr(out_1), .din(Rt_Out), .data(DataMemory_Out), .str(sw), .clk(Clk), .ld(lw));  // open: sel, clr

  // Other names for the same wires on the sheet: J_12Im[2:0] = Func; Rt[2:0] = J_12Im[5:3]; Rs[2:0] = J_12Im[8:6];
  //   Rd[2:0] = J_12Im[11:9]; Alu_Out[15:0] = out_1

  // Notes on the sheet:
  //   Program Counter
  //   Control Unit
  //   R-type
  //   Instructions Memory
  //   I-Type
  //   SW
  //   LW
  //   BNE
  //   BEQ
  //   BGT
  //   BGE
  //   BLT
  //   BLE
  //   Jump
  //   Jump and Link
  //   Load Upper Immediate
  //   J-type
  //   Register File
  //   Arithmetic Logical Unit
  //   DataMemory
endmodule

module RegisterFile (
  input  [15:0] BusW,
  input  [2:0] RB,
  input  [2:0] RA,
  input  Clock,
  input  RegWrite,
  input  [2:0] RW,
  output [15:0] BusB,
  output [15:0] BusA
);

  wire _1_out, _2_out, _3_out, _4_out, _5_out, _6_out, _7_out, decoder_1_out1, decoder_1_out2,
       decoder_1_out3, decoder_1_out4, decoder_1_out5, decoder_1_out6, decoder_1_out7, decoder_2_out0,
       decoder_2_out1, decoder_2_out2, decoder_2_out3, decoder_2_out4, decoder_2_out5, decoder_2_out6,
       decoder_2_out7, decoder_3_out0, decoder_3_out1, decoder_3_out2, decoder_3_out3, decoder_3_out4,
       decoder_3_out5, decoder_3_out6, decoder_3_out7;
  wire [15:0] R1_q, R2_q, R3_q, R4_q, R5_q, R6_q, R7_q;

  Decoder #(.select(3)) decoder_1 (
    .out1(decoder_1_out1), .out2(decoder_1_out2), .out3(decoder_1_out3), .out4(decoder_1_out4),
    .out5(decoder_1_out5), .out6(decoder_1_out6), .out7(decoder_1_out7), .sel(RW), .en(1'b1));  // open: out0
  and _1 (_1_out, decoder_1_out1, RegWrite);
  and _2 (_2_out, decoder_1_out2, RegWrite);
  and _3 (_3_out, decoder_1_out3, RegWrite);
  and _4 (_4_out, decoder_1_out4, RegWrite);
  and _5 (_5_out, decoder_1_out5, RegWrite);
  and _6 (_6_out, decoder_1_out6, RegWrite);
  and _7 (_7_out, decoder_1_out7, RegWrite);
  Register #(.width(16)) R1 (.D(BusW), .en(_1_out), .Q(R1_q), .clk(Clock));  // open: clr
  Register #(.width(16)) R2 (.D(BusW), .en(_2_out), .Q(R2_q), .clk(Clock));  // open: clr
  Register #(.width(16)) R3 (.D(BusW), .en(_3_out), .Q(R3_q), .clk(Clock));  // open: clr
  Register #(.width(16)) R4 (.D(BusW), .en(_4_out), .Q(R4_q), .clk(Clock));  // open: clr
  Register #(.width(16)) R5 (.D(BusW), .en(_5_out), .Q(R5_q), .clk(Clock));  // open: clr
  Register #(.width(16)) R6 (.D(BusW), .en(_6_out), .Q(R6_q), .clk(Clock));  // open: clr
  Register #(.width(16)) R7 (.D(BusW), .en(_7_out), .Q(R7_q), .clk(Clock));  // open: clr
  assign BusA = decoder_2_out0 ? {16{1'b0}} : 16'bz;  // Controlled_Buffer controlled_buffer_1
  assign BusA = decoder_2_out2 ? R2_q : 16'bz;  // Controlled_Buffer controlled_buffer_2
  assign BusA = decoder_2_out1 ? R1_q : 16'bz;  // Controlled_Buffer controlled_buffer_3
  Decoder #(.select(3)) decoder_2 (
    .out0(decoder_2_out0), .out1(decoder_2_out1), .out2(decoder_2_out2), .out3(decoder_2_out3),
    .out4(decoder_2_out4), .out5(decoder_2_out5), .out6(decoder_2_out6), .out7(decoder_2_out7), .sel(RA),
    .en(1'b1));
  assign BusA = decoder_2_out6 ? R6_q : 16'bz;  // Controlled_Buffer controlled_buffer_4
  assign BusA = decoder_2_out5 ? R5_q : 16'bz;  // Controlled_Buffer controlled_buffer_5
  assign BusA = decoder_2_out4 ? R4_q : 16'bz;  // Controlled_Buffer controlled_buffer_6
  assign BusA = decoder_2_out3 ? R3_q : 16'bz;  // Controlled_Buffer controlled_buffer_7
  assign BusA = decoder_2_out7 ? R7_q : 16'bz;  // Controlled_Buffer controlled_buffer_8
  assign BusB = decoder_3_out0 ? {16{1'b0}} : 16'bz;  // Controlled_Buffer controlled_buffer_9
  assign BusB = decoder_3_out3 ? R3_q : 16'bz;  // Controlled_Buffer controlled_buffer_10
  assign BusB = decoder_3_out2 ? R2_q : 16'bz;  // Controlled_Buffer controlled_buffer_11
  assign BusB = decoder_3_out1 ? R1_q : 16'bz;  // Controlled_Buffer controlled_buffer_12
  Decoder #(.select(3)) decoder_3 (
    .out0(decoder_3_out0), .out1(decoder_3_out1), .out2(decoder_3_out2), .out3(decoder_3_out3),
    .out4(decoder_3_out4), .out5(decoder_3_out5), .out6(decoder_3_out6), .out7(decoder_3_out7), .sel(RB),
    .en(1'b1));
  assign BusB = decoder_3_out7 ? R7_q : 16'bz;  // Controlled_Buffer controlled_buffer_13
  assign BusB = decoder_3_out6 ? R6_q : 16'bz;  // Controlled_Buffer controlled_buffer_14
  assign BusB = decoder_3_out5 ? R5_q : 16'bz;  // Controlled_Buffer controlled_buffer_15
  assign BusB = decoder_3_out4 ? R4_q : 16'bz;  // Controlled_Buffer controlled_buffer_16

  // Notes on the sheet:
  //   STAGE 1
  //   STAGE 2
endmodule

module ALU (
  input  [3:0] Op,
  input  [2:0] func,
  input  [15:0] Rs,
  input  [15:0] Rt,
  output [15:0] Rd
);

  wire comparator_1_eq, comparator_1_gt, comparator_2_eq, comparator_2_gt, comparator_3_eq, comparator_3_gt,
       comparator_3_lt, comparator_4_eq, comparator_4_gt, comparator_4_lt, or_2_out, or_3_out, or_4_out,
       or_5_out, or_6_out, or_7_out;
  wire [15:0] adder_1_out, adder_2_out, and_1_out, and_2_out, and_3_out, bit_extender_1_out,
       bit_extender_2_out, bit_extender_3_out, bit_extender_4_out, bit_extender_5_out, bit_extender_6_out,
       bit_extender_7_out, bit_extender_8_out, bit_extender_9_out, bit_extender_10_out, multiplexer_1_out,
       multiplexer_2_out, not_1_out, or_1_out, shifter_1_out, shifter_2_out, shifter_3_out, shifter_4_out,
       subtractor_1_out, xor_1_out;

  assign or_1_out = Rs | Rt;  // OR_Gate or_1, 16 bits wide
  assign xor_1_out = Rt ^ Rs;  // XOR_Gate xor_1, 16 bits wide
  assign and_1_out = Rt & Rs;  // AND_Gate and_1, 16 bits wide
  Adder #(.width(16)) adder_1 (.a(Rs), .b(Rt), .out(adder_1_out));  // open: cin, cout
  Subtractor #(.width(16)) subtractor_1 (.a(Rs), .b(Rt), .out(subtractor_1_out));  // open: bin, bout
  Comparator #(.width(16)) comparator_1 (.a(Rs), .b(Rt), .gt(comparator_1_gt), .eq(comparator_1_eq));  // open: lt
  Comparator #(.width(16), .mode("unsigned")) comparator_2 (
    .a(Rs), .b(Rt), .gt(comparator_2_gt), .eq(comparator_2_eq));  // open: lt
  Shifter #(.width(16)) shifter_1 (.in(Rs), .\dist (Rt[3:0]), .out(shifter_1_out));
  Shifter #(.width(16), .shift("ar")) shifter_2 (.in(Rs), .\dist (Rt[3:0]), .out(shifter_2_out));
  assign not_1_out = ~and_1_out;  // NOT_Gate not_1, 16 bits wide
  or or_2 (or_2_out, comparator_1_gt, comparator_1_eq);
  or or_3 (or_3_out, comparator_2_gt, comparator_2_eq);
  Shifter #(.width(16), .shift("lr")) shifter_3 (.in(Rs), .\dist (Rt[3:0]), .out(shifter_3_out));
  Shifter #(.width(16), .shift("rr")) shifter_4 (.in(Rs), .\dist (Rt[3:0]), .out(shifter_4_out));
  Comparator #(.width(16), .mode("unsigned")) comparator_3 (
    .a(Rt), .b({16{1'b0}}), .gt(comparator_3_gt), .eq(comparator_3_eq), .lt(comparator_3_lt));
  assign bit_extender_1_out = {{15{1'b1}}, comparator_3_eq};  // Bit_Extender bit_extender_1
  or or_4 (or_4_out, comparator_3_gt, comparator_3_lt);
  assign bit_extender_2_out = {{15{1'b0}}, or_2_out};  // Bit_Extender bit_extender_2
  assign bit_extender_3_out = {{15{1'b0}}, or_3_out};  // Bit_Extender bit_extender_3
  assign and_2_out = bit_extender_1_out & Rs;  // AND_Gate and_2, 16 bits wide
  assign bit_extender_4_out = {{15{1'b1}}, or_4_out};  // Bit_Extender bit_extender_4
  assign and_3_out = bit_extender_4_out & Rs;  // AND_Gate and_3, 16 bits wide
  Comparator #(.width(16)) comparator_4 (
    .a(Rt), .b(Rs), .gt(comparator_4_gt), .eq(comparator_4_eq), .lt(comparator_4_lt));
  Multiplexer #(.select(3), .width(16), .enable("false")) multiplexer_1 (
    .in0(or_1_out), .in1(and_1_out), .in2(not_1_out), .in3(xor_1_out), .in4(adder_1_out),
    .in5(subtractor_1_out), .in6(bit_extender_2_out), .in7(bit_extender_3_out), .out(multiplexer_1_out),
    .sel(func));
  Multiplexer #(.select(3), .width(16), .enable("false")) multiplexer_2 (
    .in0(shifter_1_out), .in1(shifter_3_out), .in2(shifter_2_out), .in3(shifter_4_out), .in4(and_2_out),
    .in5(and_3_out), .in6({16{1'b0}}), .in7({16{1'b0}}), .out(multiplexer_2_out), .sel(func));
  assign bit_extender_5_out = {{15{1'b0}}, comparator_4_eq};  // Bit_Extender bit_extender_5
  assign bit_extender_6_out = {{15{1'b0}}, or_5_out};  // Bit_Extender bit_extender_6
  or or_5 (or_5_out, comparator_4_gt, comparator_4_lt);
  assign bit_extender_7_out = {{15{1'b0}}, comparator_4_gt};  // Bit_Extender bit_extender_7
  or or_6 (or_6_out, comparator_4_gt, comparator_4_eq);
  assign bit_extender_8_out = {{15{1'b0}}, or_6_out};  // Bit_Extender bit_extender_8
  assign bit_extender_9_out = {{15{1'b0}}, comparator_4_lt};  // Bit_Extender bit_extender_9
  or or_7 (or_7_out, comparator_4_eq, comparator_4_lt);
  assign bit_extender_10_out = {{15{1'b0}}, or_7_out};  // Bit_Extender bit_extender_10
  Adder #(.width(16)) adder_2 (.a(Rs), .b(Rt), .out(adder_2_out));  // open: cin, cout
  Multiplexer #(.select(4), .width(16), .enable("false")) multiplexer_3 (
    .in0(multiplexer_1_out), .in1(multiplexer_2_out), .in2(and_1_out), .in3(or_1_out), .in4(adder_1_out),
    .in5(adder_2_out), .in6(adder_2_out), .in7(bit_extender_6_out), .in8(bit_extender_5_out),
    .in9(bit_extender_7_out), .in10(bit_extender_8_out), .in11(bit_extender_9_out),
    .in12(bit_extender_10_out), .in13({16{1'b0}}), .in14({16{1'b0}}), .in15({16{1'b0}}), .out(Rd), .sel(Op));

  // Notes on the sheet:
  //   ALU For Op = 0001
  //   SLL
  //   SRL
  //   SRA
  //   ROR
  //   MOVZ MOVN
  //   ALU For Op = 0000
  //   OR 
  //   NAND
  //   XOR
  //   ADD
  //   SUB
  //   SGE
  //   SGEU
  //   Signed
  //   Signed
endmodule
